// Logisim project Project_v4.circ as structural Verilog: 17 circuits, main circuit main
module main (
);

  _14_bit_register_file u_14_bit_register_file_1 ();  // open: Write_Data, Write_enabler, RT_Selector, Register_CLOCK, RD_Selector, Data_1_Out, RS_Selector, Data_2_Out, Register_CLEAR
  _1_bit_ALU u_1_bit_alu_1 ();  // open: a, Ain, Cin_for_adder, b, Bin, out_7, out_8, ALU_Op
  _14_bit_ALU u_14_bit_alu_1 ();  // open: a, b, Operation, Ain, Bin, S, Zero_Signal, out_9, Cin
endmodule

module _14_bit_register_file (
  input  [13:0] Write_Data,
  input  Write_enabler,
  input  [2:0] RS_Selector,
  input  [2:0] RT_Selector,
  input  Register_CLOCK,
  input  Register_CLEAR,
  input  [2:0] RD_Selector,
  output [13:0] Data_1_Out,
  output [13:0] Data_2_Out
);

  wire and_1_out, and_2_out, and_3_out, and_4_out, and_5_out, and_6_out, and_7_out, and_8_out,
       decoder_1_out0, decoder_1_out1, decoder_1_out2, decoder_1_out3, decoder_1_out4, decoder_1_out5,
       decoder_1_out6, decoder_1_out7;
  wire [13:0] inpr_q, outr_q, shanto_q, sheam_q, t0_q, tahsin_q, tanzil_q, zero_q;

  Decoder #(.select(3), .enable("false")) decoder_1 (
    .out0(decoder_1_out0), .out1(decoder_1_out1), .out2(decoder_1_out2), .out3(decoder_1_out3),
    .out4(decoder_1_out4), .out5(decoder_1_out5), .out6(decoder_1_out6), .out7(decoder_1_out7),
    .sel(RD_Selector));
  and and_1 (and_1_out, decoder_1_out0, Write_enabler);
  and and_2 (and_2_out, decoder_1_out1, Write_enabler);
  and and_3 (and_3_out, decoder_1_out2, Write_enabler);
  and and_4 (and_4_out, decoder_1_out3, Write_enabler);
  and and_5 (and_5_out, decoder_1_out4, Write_enabler);
  and and_6 (and_6_out, decoder_1_out5, Write_enabler);
  and and_7 (and_7_out, decoder_1_out6, Write_enabler);
  and and_8 (and_8_out, decoder_1_out7, Write_enabler);
  Register #(.width(14)) zero (.D({14{1'b0}}), .en(and_1_out), .Q(zero_q), .clk(Register_CLOCK), .clr(Register_CLEAR));
  Register #(.width(14)) inpr (.D(Write_Data), .en(and_2_out), .Q(inpr_q), .clk(Register_CLOCK), .clr(Register_CLEAR));
  Register #(.width(14)) outr (.D(Write_Data), .en(and_3_out), .Q(outr_q), .clk(Register_CLOCK), .clr(Register_CLEAR));
  Register #(.width(14)) shanto (
    .D(Write_Data), .en(and_4_out), .Q(shanto_q), .clk(Register_CLOCK), .clr(Register_CLEAR));
  Register #(.width(14)) sheam (
    .D(Write_Data), .en(and_5_out), .Q(sheam_q), .clk(Register_CLOCK), .clr(Register_CLEAR));
  Register #(.width(14)) t0 (.D(Write_Data), .en(and_6_out), .Q(t0_q), .clk(Register_CLOCK), .clr(Register_CLEAR));
  Register #(.width(14)) tanzil (
    .D(Write_Data), .en(and_7_out), .Q(tanzil_q), .clk(Register_CLOCK), .clr(Register_CLEAR));
  Register #(.width(14)) tahsin (
    .D(Write_Data), .en(and_8_out), .Q(tahsin_q), .clk(Register_CLOCK), .clr(Register_CLEAR));
  Multiplexer #(.select(3), .width(14), .enable("false")) multiplexer_1 (
    .in0(zero_q), .in1(inpr_q), .in2(outr_q), .in3(shanto_q), .in4(sheam_q), .in5(t0_q), .in6(tanzil_q),
    .in7(tahsin_q), .out(Data_1_Out), .sel(RS_Selector));
  Multiplexer #(.select(3), .width(14), .enable("false")) multiplexer_2 (
    .in0(zero_q), .in1(inpr_q), .in2(outr_q), .in3(shanto_q), .in4(sheam_q), .in5(t0_q), .in6(tanzil_q),
    .in7(tahsin_q), .out(Data_2_Out), .sel(RT_Selector));

  // Notes on the sheet:
  //   0
  //   1
  //   2
  //   3
  //   4
  //   5
  //   6
  //   7
  //   Group #3
endmodule

module _1_bit_ALU (
  input  a,
  input  Ain,
  input  Cin_for_adder,
  input  b,
  input  [1:0] ALU_Op,
  input  Bin,
  output out_7,
  output out_8
);

  wire adder_1_out, and_1_out, multiplexer_1_out, multiplexer_2_out, not_1_out, not_2_out, or_1_out;

  not not_1 (not_1_out, a);
  not not_2 (not_2_out, b);
  Multiplexer #(.enable("false")) multiplexer_1 (.in0(a), .in1(not_1_out), .out(multiplexer_1_out), .sel(Ain));
  Multiplexer #(.enable("false")) multiplexer_2 (.in0(b), .in1(not_2_out), .out(multiplexer_2_out), .sel(Bin));
  and and_1 (and_1_out, multiplexer_1_out, multiplexer_2_out);
  or or_1 (or_1_out, multiplexer_1_out, multiplexer_2_out);
  Adder #(.width(1)) adder_1 (
    .a(multiplexer_1_out), .b(multiplexer_2_out), .out(adder_1_out), .cin(Cin_for_adder), .cout(out_8));
  Multiplexer #(.select(2), .enable("false")) multiplexer_3 (
    .in0(and_1_out), .in1(or_1_out), .in2(adder_1_out), .out(out_7), .sel(ALU_Op));  // open: in3
endmodule

module _14_bit_ALU (
  input  Cin,
  input  [13:0] a,
  input  [13:0] b,
  input  [1:0] Operation,
  input  Ain,
  input  Bin,
  output [13:0] S,
  output Zero_Signal,
  output out_9
);

  wire n2_1_bit_alu_1_out_8, n2_1_bit_alu_2_out_8, n2_1_bit_alu_3_out_8, n2_1_bit_alu_4_out_8,
       n2_1_bit_alu_5_out_8, n2_1_bit_alu_6_out_8, n2_1_bit_alu_7_out_8, n2_1_bit_alu_8_out_8,
       n2_1_bit_alu_9_out_8, n2_1_bit_alu_10_out_8, n2_1_bit_alu_11_out_8, n2_1_bit_alu_12_out_8,
       n2_1_bit_alu_13_out_8, n2_1_bit_alu_14_out_8;

  // Probe on a
  // Probe on b
  _2_1_bit_ALU u_2_1_bit_alu_1 (
    .a(a[0]), .Ain(Ain), .Cin_for_adder(Cin), .b(b[0]), .Bin(Bin), .out_7(S[0]),
    .out_8(n2_1_bit_alu_1_out_8), .ALU_Op(Operation));
  _2_1_bit_ALU u_2_1_bit_alu_2 (
    .a(a[1]), .Ain(Ain), .Cin_for_adder(n2_1_bit_alu_1_out_8), .b(b[1]), .Bin(Bin), .out_7(S[1]),
    .out_8(n2_1_bit_alu_2_out_8), .ALU_Op(Operation));
  _2_1_bit_ALU u_2_1_bit_alu_3 (
    .a(a[2]), .Ain(Ain), .Cin_for_adder(n2_1_bit_alu_2_out_8), .b(b[2]), .Bin(Bin), .out_7(S[2]),
    .out_8(n2_1_bit_alu_3_out_8), .ALU_Op(Operation));
  _2_1_bit_ALU u_2_1_bit_alu_4 (
    .a(a[3]), .Ain(Ain), .Cin_for_adder(n2_1_bit_alu_3_out_8), .b(b[3]), .Bin(Bin), .out_7(S[3]),
    .out_8(n2_1_bit_alu_4_out_8), .ALU_Op(Operation));
  // Probe on S
  _2_1_bit_ALU u_2_1_bit_alu_5 (
    .a(a[4]), .Ain(Ain), .Cin_for_adder(n2_1_bit_alu_4_out_8), .b(b[4]), .Bin(Bin), .out_7(S[4]),
    .out_8(n2_1_bit_alu_5_out_8), .ALU_Op(Operation));
  _2_1_bit_ALU u_2_1_bit_alu_6 (
    .a(a[5]), .Ain(Ain), .Cin_for_adder(n2_1_bit_alu_5_out_8), .b(b[5]), .Bin(Bin), .out_7(S[5]),
    .out_8(n2_1_bit_alu_6_out_8), .ALU_Op(Operation));
  _2_1_bit_ALU u_2_1_bit_alu_7 (
    .a(a[6]), .Ain(Ain), .Cin_for_adder(n2_1_bit_alu_6_out_8), .b(b[6]), .Bin(Bin), .out_7(S[6]),
    .out_8(n2_1_bit_alu_7_out_8), .ALU_Op(Operation));
  _2_1_bit_ALU u_2_1_bit_alu_8 (
    .a(a[7]), .Ain(Ain), .Cin_for_adder(n2_1_bit_alu_7_out_8), .b(b[7]), .Bin(Bin), .out_7(S[7]),
    .out_8(n2_1_bit_alu_8_out_8), .ALU_Op(Operation));
  _2_1_bit_ALU u_2_1_bit_alu_9 (
    .a(a[8]), .Ain(Ain), .Cin_for_adder(n2_1_bit_alu_8_out_8), .b(b[8]), .Bin(Bin), .out_7(S[8]),
    .out_8(n2_1_bit_alu_9_out_8), .ALU_Op(Operation));
  _2_1_bit_ALU u_2_1_bit_alu_10 (
    .a(a[9]), .Ain(Ain), .Cin_for_adder(n2_1_bit_alu_9_out_8), .b(b[9]), .Bin(Bin), .out_7(S[9]),
    .out_8(n2_1_bit_alu_10_out_8), .ALU_Op(Operation));
  _2_1_bit_ALU u_2_1_bit_alu_11 (
    .a(a[10]), .Ain(Ain), .Cin_for_adder(n2_1_bit_alu_10_out_8), .b(b[10]), .Bin(Bin), .out_7(S[10]),
    .out_8(n2_1_bit_alu_11_out_8), .ALU_Op(Operation));
  _2_1_bit_ALU u_2_1_bit_alu_12 (
    .a(a[11]), .Ain(Ain), .Cin_for_adder(n2_1_bit_alu_11_out_8), .b(b[11]), .Bin(Bin), .out_7(S[11]),
    .out_8(n2_1_bit_alu_12_out_8), .ALU_Op(Operation));
  _2_1_bit_ALU u_2_1_bit_alu_13 (
    .a(a[12]), .Ain(Ain), .Cin_for_adder(n2_1_bit_alu_12_out_8), .b(b[12]), .Bin(Bin), .out_7(S[12]),
    .out_8(n2_1_bit_alu_13_out_8), .ALU_Op(Operation));
  _2_1_bit_ALU u_2_1_bit_alu_14 (
    .a(a[13]), .Ain(Ain), .Cin_for_adder(n2_1_bit_alu_13_out_8), .b(b[13]), .Bin(Bin), .out_7(S[13]),
    .out_8(n2_1_bit_alu_14_out_8), .ALU_Op(Operation));
  xor xor_1 (out_9, n2_1_bit_alu_13_out_8, n2_1_bit_alu_14_out_8);
  nor u_Zero_SIgnal (Zero_Signal, S[0], S[1], S[2], S[3], S[4], S[5], S[6], S[7], S[8], S[9], S[10], S[11], S[12], S[13]);

  // Notes on the sheet:
  //   Zero Signal
endmodule

module Datapath (
  input  Jump,
  input  in_2,
  input  [1:0] ALUop,
  input  Cin,
  input  Clear_PC,
  input  RD_RT,
  input  R_I,
  input  w_en,
  input  Reg__clr,
  input  Ain,
  input  Bin_sub,
  output [3:0] Opcode,
  output [2:0] Source_1,
  output [2:0] Source_2,
  output [3:0] Destination_shamt,
  output [13:0] Data1,
  output Shamt,
  output [2:0] destination,
  output Overflow,
  output [13:0] ALU_res,
  output Overflow_2,
  output [13:0] Data1_2
);

  wire beq_cont_out, Clock_out, out_dec2_1_a_2, out_dec2_1_b_2, out_dec2_1_c, out_dec2_1_d, out_dec2_1_e,
       out_dec2_1_f, out_dec2_1_g, out_dec_1_a_2, out_dec_1_b_2, out_dec_1_c_2, out_dec_1_d_2, out_dec_1_e,
       out_dec_1_f, out_dec_1_g, out_dec_2_a_2, out_dec_2_b_2, out_dec_2_c_2, out_dec_2_d_2, out_dec_2_e,
       out_dec_2_f, out_dec_2_g, out_dec_3_a_2, out_dec_3_b_2, out_dec_3_c_2, out_dec_3_d_2, out_dec_3_e,
       out_dec_3_f, out_dec_3_g;
  wire [2:0] multiplexer_3_out;
  wire [11:4] rom_1_data;
  wire [13:0] adder_1_out, adder_2_out, bit_extender_1_out, bit_extender_4_out, multiplexer_1_out,
       multiplexer_2_out, n14_bit_register_file_1_data_1_out, n14_bit_register_file_1_data_2_out, PC_q;

  Multiplexer #(.width(14), .enable("false")) multiplexer_1 (
    .in0(adder_1_out), .in1(multiplexer_2_out), .out(multiplexer_1_out), .sel(Jump));
  Register #(.width(14)) PC (.D(multiplexer_1_out), .Q(PC_q), .clk(Clock_out), .clr(Clear_PC));  // open: en
  Clock Clock (.out(Clock_out));
  Adder #(.width(14)) adder_1 (.a(14'h1), .b(PC_q), .out(adder_1_out));  // open: cin, cout
  ROM #(.addrWidth(14), .dataWidth(16)) rom_1 (
    .addr(PC_q), .data({Opcode, rom_1_data, destination, Destination_shamt[0]}));  // open: sel
  assign bit_extender_1_out = {{4{1'b0}}, {Source_1, Source_2, destination, Destination_shamt[0]}};  // Bit_Extender bit_extender_1
  Adder #(.width(14)) adder_2 (.a(adder_1_out), .b(bit_extender_1_out), .out(adder_2_out));  // open: cin, cout
  Bit_Extender #(.in_width(4), .out_width(3)) bit_extender_2 (.in(rom_1_data[11:8]), .out(Source_1));
  Bit_Extender #(.in_width(4), .out_width(3)) bit_extender_3 (.in(rom_1_data[7:4]), .out(Source_2));
  Multiplexer #(.width(14), .enable("false")) multiplexer_2 (
    .in0(adder_1_out), .in1(adder_2_out), .out(multiplexer_2_out), .sel(beq_cont_out));
  Multiplexer #(.width(3), .enable("false")) multiplexer_3 (
    .in0(destination), .in1(Source_2), .out(multiplexer_3_out), .sel(RD_RT));
  assign bit_extender_4_out = {{10{1'b0}}, {destination, Destination_shamt[0]}};  // Bit_Extender bit_extender_4
  _14_bit_register_file u_14_bit_register_file_1 (
    .Write_enabler(w_en), .RT_Selector(Source_2), .Register_CLOCK(Clock_out),
    .RD_Selector(multiplexer_3_out), .Data_1_Out(n14_bit_register_file_1_data_1_out), .RS_Selector(Source_1),
    .Data_2_Out(n14_bit_register_file_1_data_2_out), .Register_CLEAR(Reg__clr));  // open: Write_Data
  // Probe on ALU_res
  Multiplexer #(.width(14), .enable("false")) multiplexer_4 (
    .in0(n14_bit_register_file_1_data_2_out), .in1(bit_extender_4_out), .out(Data1_2), .sel(R_I));
  out_dec out_dec_1 (
    .A(ALU_res[7]), .B(ALU_res[6]), .C(ALU_res[5]), .D(ALU_res[4]), .a_2(out_dec_1_a_2), .b_2(out_dec_1_b_2),
    .c_2(out_dec_1_c_2), .d_2(out_dec_1_d_2), .e(out_dec_1_e), .f(out_dec_1_f), .g(out_dec_1_g));
  out_dec out_dec_2 (
    .A(ALU_res[3]), .B(ALU_res[2]), .C(ALU_res[1]), .D(ALU_res[0]), .a_2(out_dec_2_a_2), .b_2(out_dec_2_b_2),
    .c_2(out_dec_2_c_2), .d_2(out_dec_2_d_2), .e(out_dec_2_e), .f(out_dec_2_f), .g(out_dec_2_g));
  // Probe on Data1_2
  _14_bit_ALU u_14_bit_alu_1 (
    .a(n14_bit_register_file_1_data_1_out), .b(Data1_2), .Operation(ALUop), .Ain(Ain), .Bin(Bin_sub),
    .S(ALU_res), .Zero_Signal(Overflow), .out_9(Overflow_2), .Cin(Cin));
  out_dec2 out_dec2_1 (
    .A(ALU_res[13]), .B(ALU_res[12]), .a_2(out_dec2_1_a_2), .b_2(out_dec2_1_b_2), .c(out_dec2_1_c),
    .d(out_dec2_1_d), .e(out_dec2_1_e), .f(out_dec2_1_f), .g(out_dec2_1_g));
  out_dec out_dec_3 (
    .A(ALU_res[11]), .B(ALU_res[10]), .C(ALU_res[9]), .D(ALU_res[8]), .a_2(out_dec_3_a_2),
    .b_2(out_dec_3_b_2), .c_2(out_dec_3_c_2), .d_2(out_dec_3_d_2), .e(out_dec_3_e), .f(out_dec_3_f),
    .g(out_dec_3_g));
  and beq_cont (beq_cont_out, in_2, Overflow);
  // Probe on ALU_res
  _7_Segment_Display u_7_segment_display_1 (
    .g(out_dec2_1_g), .f(out_dec2_1_f), .a(out_dec2_1_a_2), .b(out_dec2_1_b_2), .e(out_dec2_1_e),
    .d(out_dec2_1_d), .c(out_dec2_1_c));  // open: dp
  _7_Segment_Display u_7_segment_display_2 (
    .g(out_dec_3_g), .f(out_dec_3_f), .a(out_dec_3_a_2), .b(out_dec_3_b_2), .e(out_dec_3_e),
    .d(out_dec_3_d_2), .c(out_dec_3_c_2));  // open: dp
  _7_Segment_Display u_7_segment_display_3 (
    .g(out_dec_2_g), .f(out_dec_2_f), .a(out_dec_2_a_2), .b(out_dec_2_b_2), .e(out_dec_2_e),
    .d(out_dec_2_d_2), .c(out_dec_2_c_2));  // open: dp
  _7_Segment_Display u_7_segment_display_4 (
    .g(out_dec_1_g), .f(out_dec_1_f), .a(out_dec_1_a_2), .b(out_dec_1_b_2), .e(out_dec_1_e),
    .d(out_dec_1_d_2), .c(out_dec_1_c_2));  // open: dp

  assign Data1 = ALU_res;
  assign Destination_shamt[3:1] = destination;
  assign Shamt = Destination_shamt[0];

  // Notes on the sheet:
  //   contents of rom_1 (hex, n*v repeats v):
  //   1238 9054 7366 5793 abcd
  //   add t0, shanto, sheam
  //   0010 101 011 100 0
endmodule

module out_dec (
  input  A,
  input  B,
  input  C,
  input  D,
  output a_2,
  output b_2,
  output c_2,
  output d_2,
  output e,
  output f,
  output g
);

  wire and_1_out, and_2_out, and_3_out, and_4_out, and_5_out, and_6_out, and_7_out, and_8_out, and_9_out,
       and_10_out, and_11_out, and_12_out, and_13_out, and_14_out, and_15_out, and_16_out, and_17_out,
       and_18_out, and_19_out, and_20_out, and_21_out, and_22_out, and_23_out, and_24_out, and_25_out,
       and_26_out, and_27_out, and_28_out, and_29_out, and_30_out, and_31_out, and_32_out, and_33_out,
       not_1_out, not_2_out, not_3_out, not_4_out, not_5_out, not_6_out, not_7_out, not_8_out, not_9_out,
       not_10_out, not_11_out, not_12_out, not_13_out, not_14_out, not_15_out, not_16_out, not_17_out,
       not_18_out, not_19_out, not_20_out, not_21_out, not_22_out, not_23_out, not_24_out, not_25_out,
       not_26_out, not_27_out, not_28_out, not_29_out, not_30_out, not_31_out, not_32_out, not_33_out,
       not_34_out, not_35_out, not_36_out, not_37_out, not_38_out, not_39_out, not_40_out, not_41_out,
       not_42_out;

  not not_1 (not_1_out, A);
  and and_1 (and_1_out, not_1_out, not_2_out, not_3_out);
  not not_2 (not_2_out, B);
  not not_3 (not_3_out, D);
  not not_4 (not_4_out, A);
  and and_2 (and_2_out, not_4_out, C);
  not not_5 (not_5_out, A);
  and and_3 (and_3_out, not_5_out, B, D);
  and and_4 (and_4_out, B, C);
  and and_5 (and_5_out, A, not_6_out, not_7_out);
  not not_6 (not_6_out, B);
  not not_7 (not_7_out, C);
  not not_8 (not_8_out, A);
  not not_9 (not_9_out, B);
  not not_10 (not_10_out, A);
  not not_11 (not_11_out, C);
  not not_12 (not_12_out, D);
  not not_13 (not_13_out, B);
  not not_14 (not_14_out, C);
  not not_15 (not_15_out, A);
  not not_16 (not_16_out, C);
  not not_17 (not_17_out, D);
  not not_18 (not_18_out, A);
  and and_6 (and_6_out, not_18_out, not_19_out);
  not not_19 (not_19_out, C);
  not not_20 (not_20_out, A);
  and and_7 (and_7_out, not_20_out, D);
  not not_21 (not_21_out, C);
  and and_8 (and_8_out, not_21_out, D);
  not not_22 (not_22_out, A);
  and and_9 (and_9_out, not_22_out, B);
  and and_10 (and_10_out, A, not_23_out);
  not not_23 (not_23_out, B);
  not not_24 (not_24_out, B);
  and and_11 (and_11_out, not_24_out, not_25_out);
  not not_25 (not_25_out, D);
  not not_26 (not_26_out, B);
  and and_12 (and_12_out, not_26_out, C);
  and and_13 (and_13_out, C, not_27_out);
  not not_27 (not_27_out, D);
  and and_14 (and_14_out, B, not_28_out, D);
  not not_28 (not_28_out, C);
  and and_15 (and_15_out, A, not_29_out);
  not not_29 (not_29_out, C);
  not not_30 (not_30_out, B);
  and and_16 (and_16_out, not_30_out, not_31_out);
  not not_31 (not_31_out, D);
  and and_17 (and_17_out, C, not_32_out);
  not not_32 (not_32_out, D);
  and and_18 (and_18_out, A, C);
  and and_19 (and_19_out, A, B);
  not not_33 (not_33_out, B);
  not not_34 (not_34_out, C);
  and and_20 (and_20_out, not_33_out, not_34_out, not_35_out);
  not not_35 (not_35_out, D);
  not not_36 (not_36_out, A);
  and and_21 (and_21_out, not_36_out, B, not_37_out);
  not not_37 (not_37_out, C);
  and and_22 (and_22_out, B, C, not_38_out);
  not not_38 (not_38_out, D);
  not not_39 (not_39_out, B);
  and and_23 (and_23_out, A, not_39_out, D);
  and and_24 (and_24_out, A, B, C);
  not not_40 (not_40_out, B);
  and and_25 (and_25_out, not_40_out, C);
  and and_26 (and_26_out, B, not_41_out);
  not not_41 (not_41_out, C);
  and and_27 (and_27_out, B, not_42_out);
  not not_42 (not_42_out, D);
  or or_1 (a_2, and_1_out, and_2_out, and_3_out, and_4_out, and_5_out);
  and and_28 (and_28_out, not_8_out, not_9_out);
  and and_29 (and_29_out, not_10_out, not_11_out, not_12_out);
  and and_30 (and_30_out, not_13_out, not_14_out);
  and and_31 (and_31_out, not_15_out, C, D);
  and and_32 (and_32_out, A, not_16_out, D);
  and and_33 (and_33_out, A, B, C, not_17_out);
  or or_2 (c_2, and_6_out, and_7_out, and_8_out, and_9_out, and_10_out);
  or or_3 (d_2, and_11_out, and_12_out, and_13_out, and_14_out, and_15_out);
  or or_4 (e, and_16_out, and_17_out, and_18_out, and_19_out);
  or or_5 (f, and_20_out, and_21_out, and_22_out, and_23_out, and_24_out);
  or or_6 (g, and_25_out, and_26_out, and_27_out, A);
  or or_7 (b_2, and_28_out, and_29_out, and_30_out, and_31_out, and_32_out, and_33_out);
endmodule

module out_dec2 (
  input  A,
  input  B,
  output a_2,
  output b_2,
  output c,
  output d,
  output e,
  output f,
  output g
);

  wire not_1_out, not_2_out, not_3_out, not_5_out, not_6_out;

  not not_1 (not_1_out, B);
  not not_2 (not_2_out, A);
  not not_3 (not_3_out, B);
  not not_4 (e, B);
  not not_5 (not_5_out, A);
  not not_6 (not_6_out, B);
  or or_1 (a_2, not_1_out, A);
  or or_2 (c, not_2_out, B);
  or or_3 (d, not_3_out, A);
  and and_1 (f, not_5_out, not_6_out);

  assign b_2 = 1'b1;
  assign g = A;
endmodule

module display (
  input  in_1,
  input  in_2,
  input  in_3,
  input  in_4,
  input  in_5,
  input  in_6,
  input  in_7,
  input  in_8,
  input  in_9,
  input  in_10,
  input  in_11,
  input  in_12,
  input  in_13,
  input  in_14,
  output out_15,
  output out_16,
  output out_17,
  output out_18,
  output out_19,
  output out_20,
  output out_21,
  output out_22,
  output out_23,
  output out_24,
  output out_25,
  output out_26,
  output out_27,
  output out_28,
  output out_29,
  output out_30,
  output out_31,
  output out_32,
  output out_33,
  output out_34,
  output out_35,
  output out_36,
  output out_37,
  output out_38,
  output out_39,
  output out_40,
  output out_41,
  output out_42
);

  out_dec2 out_dec2_1 (
    .A(in_2), .B(in_1), .a_2(out_15), .b_2(out_16), .c(out_17), .d(out_18), .e(out_19), .f(out_20), .g(out_21));
  out_dec out_dec_1 (
    .A(in_6), .B(in_5), .C(in_4), .D(in_3), .a_2(out_22), .b_2(out_23), .c_2(out_24), .d_2(out_25),
    .e(out_26), .f(out_27), .g(out_28));
  out_dec out_dec_2 (
    .A(in_10), .B(in_9), .C(in_8), .D(in_7), .a_2(out_29), .b_2(out_30), .c_2(out_31), .d_2(out_32),
    .e(out_33), .f(out_34), .g(out_35));
  out_dec out_dec_3 (
    .A(in_14), .B(in_13), .C(in_12), .D(in_11), .a_2(out_36), .b_2(out_37), .c_2(out_38), .d_2(out_39),
    .e(out_40), .f(out_41), .g(out_42));
endmodule

module copy (
  input  Jump,
  input  in_2,
  input  [1:0] ALUop,
  input  Cin,
  input  Clear_PC,
  input  RD_RT,
  input  R_I,
  input  w_en,
  input  Reg__clr,
  input  Ain,
  input  Bin_sub,
  input  ALU_Ld_st,
  input  store,
  input  load,
  output [3:0] Opcode,
  output [2:0] Source_1,
  output [2:0] Source_2,
  output [3:0] Destination_shamt,
  output [13:0] Data1,
  output Shamt,
  output [2:0] destination,
  output Overflow,
  output [13:0] ALU_res,
  output Overflow_2,
  output [13:0] Data1_2,
  output [13:0] Data1_3
);

  wire beq_cont_out, Clock_out, display_1_out_15, display_1_out_16, display_1_out_17, display_1_out_18,
       display_1_out_19, display_1_out_20, display_1_out_21, display_1_out_22, display_1_out_23,
       display_1_out_24, display_1_out_25, display_1_out_26, display_1_out_27, display_1_out_28,
       display_1_out_29, display_1_out_30, display_1_out_31, display_1_out_32, display_1_out_33,
       display_1_out_34, display_1_out_35, display_1_out_36, display_1_out_37, display_1_out_38,
       display_1_out_39, display_1_out_40, display_1_out_41, display_1_out_42;
  wire [2:0] multiplexer_3_out;
  wire [11:4] rom_1_data;
  wire [13:0] adder_1_out, adder_2_out, bit_extender_1_out, bit_extender_4_out, multiplexer_1_out,
       multiplexer_2_out, multiplexer_5_out, n14_bit_register_file_1_data_2_out, PC_q, register_1_q;

  Multiplexer #(.width(14), .enable("false")) multiplexer_1 (
    .in0(adder_1_out), .in1(multiplexer_2_out), .out(multiplexer_1_out), .sel(Jump));
  Register #(.width(14)) PC (.D(multiplexer_1_out), .Q(PC_q), .clk(Clock_out), .clr(Clear_PC));  // open: en
  Clock Clock (.out(Clock_out));
  Adder #(.width(14)) adder_1 (.a(14'h1), .b(PC_q), .out(adder_1_out));  // open: cin, cout
  ROM #(.addrWidth(14), .dataWidth(16)) rom_1 (
    .addr(PC_q), .data({Opcode, rom_1_data, destination, Destination_shamt[0]}));  // open: sel
  assign bit_extender_1_out = {{4{1'b0}}, {Source_1, Source_2, destination, Destination_shamt[0]}};  // Bit_Extender bit_extender_1
  Adder #(.width(14)) adder_2 (.a(adder_1_out), .b(bit_extender_1_out), .out(adder_2_out));  // open: cin, cout
  Bit_Extender #(.in_width(4), .out_width(3)) bit_extender_2 (.in(rom_1_data[11:8]), .out(Source_1));
  Bit_Extender #(.in_width(4), .out_width(3)) bit_extender_3 (.in(rom_1_data[7:4]), .out(Source_2));
  Multiplexer #(.width(14), .enable("false")) multiplexer_2 (
    .in0(adder_1_out), .in1(adder_2_out), .out(multiplexer_2_out), .sel(beq_cont_out));
  Multiplexer #(.width(3), .enable("false")) multiplexer_3 (
    .in0(destination), .in1(Source_2), .out(multiplexer_3_out), .sel(RD_RT));
  assign bit_extender_4_out = {{10{1'b0}}, {destination, Destination_shamt[0]}};  // Bit_Extender bit_extender_4
  Register #(.width(14)) register_1 (.Q(register_1_q));  // open: D, en, clk, clr
  _14_bit_register_file u_14_bit_register_file_1 (
    .Write_Data(multiplexer_5_out), .Write_enabler(w_en), .RT_Selector(Source_2), .Register_CLOCK(Clock_out),
    .RD_Selector(multiplexer_3_out), .Data_1_Out(Data1), .RS_Selector(Source_1),
    .Data_2_Out(n14_bit_register_file_1_data_2_out), .Register_CLEAR(Reg__clr));
  // Probe on Data1
  Multiplexer #(.width(14), .enable("false")) multiplexer_4 (
    .in0(n14_bit_register_file_1_data_2_out), .in1(bit_extender_4_out), .out(Data1_3), .sel(R_I));
  // Probe on Data1_3
  display display_1 (
    .in_1(register_1_q[12]), .in_2(register_1_q[13]), .out_15(display_1_out_15), .out_16(display_1_out_16),
    .out_17(display_1_out_17), .out_18(display_1_out_18), .out_19(display_1_out_19),
    .out_20(display_1_out_20), .out_21(display_1_out_21), .out_22(display_1_out_22),
    .out_23(display_1_out_23), .out_24(display_1_out_24), .out_25(display_1_out_25),
    .out_26(display_1_out_26), .out_27(display_1_out_27), .out_28(display_1_out_28),
    .out_29(display_1_out_29), .out_30(display_1_out_30), .out_31(display_1_out_31),
    .out_32(display_1_out_32), .out_33(display_1_out_33), .out_34(display_1_out_34),
    .out_35(display_1_out_35), .out_36(display_1_out_36), .out_37(display_1_out_37),
    .out_38(display_1_out_38), .out_39(display_1_out_39), .out_40(display_1_out_40),
    .out_41(display_1_out_41), .out_42(display_1_out_42), .in_3(register_1_q[8]), .in_4(register_1_q[9]),
    .in_5(register_1_q[10]), .in_6(register_1_q[11]), .in_7(register_1_q[4]), .in_8(register_1_q[5]),
    .in_9(register_1_q[6]), .in_10(register_1_q[7]), .in_11(register_1_q[0]), .in_12(register_1_q[1]),
    .in_13(register_1_q[2]), .in_14(register_1_q[3]));
  _14_bit_ALU u_14_bit_alu_1 (
    .a(Data1), .b(Data1_3), .Operation(ALUop), .Ain(Ain), .Bin(Bin_sub), .S(ALU_res), .Zero_Signal(Overflow),
    .out_9(Overflow_2), .Cin(Cin));
  _7_Segment_Display u_7_segment_display_1 (
    .g(display_1_out_21), .f(display_1_out_20), .a(display_1_out_15), .b(display_1_out_16),
    .e(display_1_out_19), .d(display_1_out_18), .c(display_1_out_17));  // open: dp
  and beq_cont (beq_cont_out, in_2, Overflow);
  // Probe on ALU_res
  _7_Segment_Display u_7_segment_display_2 (
    .g(display_1_out_28), .f(display_1_out_27), .a(display_1_out_22), .b(display_1_out_23),
    .e(display_1_out_26), .d(display_1_out_25), .c(display_1_out_24));  // open: dp
  _7_Segment_Display u_7_segment_display_3 (
    .g(display_1_out_35), .f(display_1_out_34), .a(display_1_out_29), .b(display_1_out_30),
    .e(display_1_out_33), .d(display_1_out_32), .c(display_1_out_31));  // open: dp
  RAM #(.addrWidth(14), .dataWidth(14), .bus("separate")) ram_1 (
    .addr(ALU_res), .din(n14_bit_register_file_1_data_2_out), .data(Data1_2), .str(store), .clk(Clock_out),
    .ld(load));  // open: sel, clr
  _7_Segment_Display u_7_segment_display_4 (
    .g(display_1_out_42), .f(display_1_out_41), .a(display_1_out_36), .b(display_1_out_37),
    .e(display_1_out_40), .d(display_1_out_39), .c(display_1_out_38));  // open: dp
  // Probe on Data1_2
  Multiplexer #(.width(14), .enable("false")) multiplexer_5 (
    .in0(ALU_res), .in1(Data1_2), .out(multiplexer_5_out), .sel(ALU_Ld_st));

  assign Destination_shamt[3:1] = destination;
  assign Shamt = Destination_shamt[0];

  // Notes on the sheet:
  //   contents of rom_1 (hex, n*v repeats v):
  //   234e 9655 e005
  //   add t0, shanto, sheam
  //   0010 101 011 100 0
endmodule

module ex2 (
  input  Jump,
  input  in_2,
  input  [1:0] ALUop,
  input  Cin,
  input  Clear_PC,
  input  RD_RT,
  input  R_I,
  input  w_en,
  input  Reg__clr,
  input  Ain,
  input  Bin_sub,
  input  ALU_Ld_st,
  input  store,
  input  load,
  output [3:0] Opcode,
  output [2:0] Source_1,
  output [2:0] Source_2,
  output [3:0] Destination_shamt,
  output [13:0] Data1,
  output Shamt,
  output [2:0] destination,
  output Zero,
  output [13:0] ALU_res,
  output Overflow,
  output [13:0] Data1_2,
  output [13:0] Data1_3
);

  wire beq_cont_out, Clock_out;
  wire [2:0] multiplexer_2_out;
  wire [3:0] a;
  wire [11:4] rom_1_data;
  wire [13:0] adder_1_out, adder_2_out, bit_extender_1_out, bit_extender_4_out, multiplexer_1_out,
       multiplexer_3_out, multiplexer_5_out, n14_bit_register_file_1_data_2_out, PC_q;

  Multiplexer #(.width(14), .enable("false")) multiplexer_1 (
    .in0(adder_1_out), .in1(multiplexer_3_out), .out(multiplexer_1_out), .sel(Jump));
  Register #(.width(14)) PC (.D(multiplexer_1_out), .Q(PC_q), .clk(Clock_out), .clr(Clear_PC));  // open: en
  Clock Clock (.out(Clock_out));
  Adder #(.width(14)) adder_1 (.a(14'h1), .b(PC_q), .out(adder_1_out));  // open: cin, cout
  ROM #(.addrWidth(14), .dataWidth(16)) rom_1 (
    .addr(PC_q), .data({Opcode, rom_1_data, destination, Destination_shamt[0]}));  // open: sel
  assign bit_extender_1_out = {{4{1'b0}}, {Source_1, Source_2, destination, Destination_shamt[0]}};  // Bit_Extender bit_extender_1
  Adder #(.width(14)) adder_2 (.a(adder_1_out), .b(bit_extender_1_out), .out(adder_2_out));  // open: cin, cout
  Bit_Extender #(.in_width(4), .out_width(3)) bit_extender_2 (.in(rom_1_data[11:8]), .out(Source_1));
  Bit_Extender #(.in_width(4), .out_width(3)) bit_extender_3 (.in(rom_1_data[7:4]), .out(Source_2));
  Multiplexer #(.width(3), .enable("false")) multiplexer_2 (
    .in0(destination), .in1(Source_2), .out(multiplexer_2_out), .sel(RD_RT));
  assign bit_extender_4_out = {{10{1'b0}}, {destination, Destination_shamt[0]}};  // Bit_Extender bit_extender_4
  Multiplexer #(.width(14), .enable("false")) multiplexer_3 (
    .in0(adder_1_out), .in1(adder_2_out), .out(multiplexer_3_out), .sel(beq_cont_out));
  _14_bit_register_file u_14_bit_register_file_1 (
    .Write_Data(multiplexer_5_out), .Write_enabler(w_en), .RT_Selector(Source_2), .Register_CLOCK(Clock_out),
    .RD_Selector(multiplexer_2_out), .Data_1_Out(Data1), .RS_Selector(Source_1),
    .Data_2_Out(n14_bit_register_file_1_data_2_out), .Register_CLEAR(Reg__clr));
  Hex_Digit_Display hex_digit_display_1 (.value(a));  // open: dp
  Hex_Digit_Display hex_digit_display_2 (.value(ALU_res[11:8]));  // open: dp
  Multiplexer #(.width(14), .enable("false")) multiplexer_4 (
    .in0(n14_bit_register_file_1_data_2_out), .in1(bit_extender_4_out), .out(Data1_3), .sel(R_I));
  Hex_Digit_Display hex_digit_display_3 (.value(ALU_res[7:4]));  // open: dp
  Hex_Digit_Display hex_digit_display_4 (.value(ALU_res[3:0]));  // open: dp
  // Probe on Data1
  // Probe on Data1_3
  _14_bit_ALU u_14_bit_alu_1 (
    .a(Data1), .b(Data1_3), .Operation(ALUop), .Ain(Ain), .Bin(Bin_sub), .S(ALU_res), .Zero_Signal(Zero),
    .out_9(Overflow), .Cin(Cin));
  and beq_cont (beq_cont_out, in_2, Zero);
  // Probe on ALU_res
  RAM #(.addrWidth(14), .dataWidth(14), .bus("separate")) ram_1 (
    .addr(ALU_res), .din(n14_bit_register_file_1_data_2_out), .data(Data1_2), .str(store), .clk(Clock_out),
    .ld(load));  // open: sel, clr
  // Probe on Data1_2
  Multiplexer #(.width(14), .enable("false")) multiplexer_5 (
    .in0(ALU_res), .in1(Data1_2), .out(multiplexer_5_out), .sel(ALU_Ld_st));
  assign a = {{2{1'b0}}, ALU_res[13:12]};  // Bit_Extender bit_extender_5

  assign Destination_shamt[3:1] = destination;
  assign Shamt = Destination_shamt[0];

  // Other names for the same wires on the sheet: ALU_tunner[13:0] = ALU_res; b[3:0] = ALU_res[11:8];
  //   c[3:0] = ALU_res[7:4]; d[3:0] = ALU_res[3:0]

  // Notes on the sheet:
  //   contents of rom_1 (hex, n*v repeats v):
  //   234e 9655 e005
  //   add t0, shanto, sheam
  //   0010 101 011 100 0
endmodule

module ex3 (
  input  Jump,
  input  in_2,
  input  [1:0] ALUop,
  input  Cin,
  input  Clear_PC,
  input  RD_RT,
  input  R_I,
  input  w_en,
  input  Reg__clr,
  input  Ain,
  input  Bin_sub,
  input  [13:0] load,
  input  ALU_Ld_st,
  input  store,
  input  load_2,
  output [3:0] Opcode,
  output [2:0] Source_1,
  output [2:0] Source_2,
  output [3:0] Destination_shamt,
  output [13:0] Data1,
  output Shamt,
  output [2:0] destination,
  output Overflow,
  output [13:0] ALU_res,
  output Overflow_2,
  output [13:0] Data1_2,
  output [13:0] Data1_3
);

  wire beq_cont_out, Clock_out, undriven;
  wire [2:0] multiplexer_3_out;
  wire [3:0] a;
  wire [11:4] rom_1_data;
  wire [13:0] adder_1_out, adder_2_out, bit_extender_1_out, bit_extender_4_out, multiplexer_1_out,
       multiplexer_2_out, multiplexer_4_out, multiplexer_6_out, n14_bit_register_file_1_data_2_out, PC_q;

  Multiplexer #(.width(14), .enable("false")) multiplexer_1 (
    .in0(adder_1_out), .in1(multiplexer_4_out), .out(multiplexer_1_out), .sel(Jump));
  Register #(.width(14)) PC (.D(multiplexer_1_out), .Q(PC_q), .clk(Clock_out), .clr(Clear_PC));  // open: en
  Clock Clock (.out(Clock_out));
  Adder #(.width(14)) adder_1 (.a(14'h1), .b(PC_q), .out(adder_1_out));  // open: cin, cout
  ROM #(.addrWidth(14), .dataWidth(16)) rom_1 (
    .addr(PC_q), .data({Opcode, rom_1_data, destination, Destination_shamt[0]}));  // open: sel
  Multiplexer #(.width(14), .enable("false")) multiplexer_2 (
    .in0(load), .in1(multiplexer_6_out), .out(multiplexer_2_out), .sel(undriven));
  assign bit_extender_1_out = {{4{1'b0}}, {Source_1, Source_2, destination, Destination_shamt[0]}};  // Bit_Extender bit_extender_1
  Adder #(.width(14)) adder_2 (.a(adder_1_out), .b(bit_extender_1_out), .out(adder_2_out));  // open: cin, cout
  Bit_Extender #(.in_width(4), .out_width(3)) bit_extender_2 (.in(rom_1_data[11:8]), .out(Source_1));
  Bit_Extender #(.in_width(4), .out_width(3)) bit_extender_3 (.in(rom_1_data[7:4]), .out(Source_2));
  Multiplexer #(.width(3), .enable("false")) multiplexer_3 (
    .in0(destination), .in1(Source_2), .out(multiplexer_3_out), .sel(RD_RT));
  assign bit_extender_4_out = {{10{1'b0}}, {destination, Destination_shamt[0]}};  // Bit_Extender bit_extender_4
  Multiplexer #(.width(14), .enable("false")) multiplexer_4 (
    .in0(adder_1_out), .in1(adder_2_out), .out(multiplexer_4_out), .sel(beq_cont_out));
  _14_bit_register_file u_14_bit_register_file_1 (
    .Write_Data(multiplexer_2_out), .Write_enabler(w_en), .RT_Selector(Source_2), .Register_CLOCK(Clock_out),
    .RD_Selector(multiplexer_3_out), .Data_1_Out(Data1), .RS_Selector(Source_1),
    .Data_2_Out(n14_bit_register_file_1_data_2_out), .Register_CLEAR(Reg__clr));
  Hex_Digit_Display hex_digit_display_1 (.value(a));  // open: dp
  Hex_Digit_Display hex_digit_display_2 (.value(ALU_res[11:8]));  // open: dp
  Multiplexer #(.width(14), .enable("false")) multiplexer_5 (
    .in0(n14_bit_register_file_1_data_2_out), .in1(bit_extender_4_out), .out(Data1_3), .sel(R_I));
  Hex_Digit_Display hex_digit_display_3 (.value(ALU_res[3:0]));  // open: dp
  Hex_Digit_Display hex_digit_display_4 (.value(ALU_res[7:4]));  // open: dp
  // Probe on Data1
  // Probe on Data1_3
  _14_bit_ALU u_14_bit_alu_1 (
    .a(Data1), .b(Data1_3), .Operation(ALUop), .Ain(Ain), .Bin(Bin_sub), .S(ALU_res), .Zero_Signal(Overflow),
    .out_9(Overflow_2), .Cin(Cin));
  and beq_cont (beq_cont_out, in_2, Overflow);
  // Probe on ALU_res
  RAM #(.addrWidth(14), .dataWidth(14), .bus("separate")) ram_1 (
    .addr(ALU_res), .din(n14_bit_register_file_1_data_2_out), .data(Data1_2), .str(store), .clk(Clock_out),
    .ld(load_2));  // open: sel, clr
  // Probe on Data1_2
  Multiplexer #(.width(14), .enable("false")) multiplexer_6 (
    .in0(ALU_res), .in1(Data1_2), .out(multiplexer_6_out), .sel(ALU_Ld_st));
  assign a = {{2{1'b0}}, ALU_res[13:12]};  // Bit_Extender bit_extender_5

  assign Destination_shamt[3:1] = destination;
  assign Shamt = Destination_shamt[0];

  // Other names for the same wires on the sheet: ALU_tunner[13:0] = ALU_res; b[3:0] = ALU_res[11:8];
  //   c[3:0] = ALU_res[7:4]; d[3:0] = ALU_res[3:0]

  // Notes on the sheet:
  //   contents of rom_1 (hex, n*v repeats v):
  //   234e 9655 e005
  //   add t0, shanto, sheam
  //   0010 101 011 100 0
endmodule

module control_2 (
  input  A_op3,
  input  B_op2,
  input  C_op1,
  input  D_op0,
  output ALU_1,
  output ALU_0,
  output AIN,
  output BIN,
  output CIN,
  output LW,
  output SW,
  output RES_RAM1,
  output RES_RAM0,
  output BEQ,
  output J,
  output WRITE_ENABLE,
  output R_I
);

  wire A_prime_B_prime_C_out, A_prime_B_prime_CD_2_out, A_prime_B_prime_CD_out, A_prime_B_prime_CD_prime_out,
       A_prime_BCD_prime_out, A_prime_BDC_prime_out, A_prime_C_prime_out, A_prime_D_prime_out,
       AB_prime_C_out, AB_prime_CD_prime_out, AB_prime_D_out, ABD_out, AC_prime_out, ACD_2_out, AD_out,
       BC_prime_D_out, op0_prime_out, op1_prime_out, op2_prime_out, op3_prime_out;

  not op3_prime (op3_prime_out, A_op3);
  not op2_prime (op2_prime_out, B_op2);
  not op1_prime (op1_prime_out, C_op1);
  not op0_prime (op0_prime_out, D_op0);
  and AB_prime_D (AB_prime_D_out, A_op3, op2_prime_out, D_op0);
  and AB_prime_C (AB_prime_C_out, A_op3, op2_prime_out, C_op1);
  and AD (AD_out, A_op3, D_op0);
  // AND_Gate AC has open pins: in0=A_op3, in1=C_op1, out=open
  // AND_Gate AB has open pins: in0=A_op3, in1=B_op2, out=open
  and AC_prime (AC_prime_out, A_op3, op1_prime_out);
  and A_prime_B_prime_C (A_prime_B_prime_C_out, op3_prime_out, op2_prime_out, C_op1);
  and A_prime_C_prime_D (ALU_0, op3_prime_out, op1_prime_out, D_op0);
  and A_prime_BC_prime (AIN, op3_prime_out, B_op2, op1_prime_out);
  and BC_prime_D (BC_prime_D_out, B_op2, op1_prime_out, D_op0);
  and A_prime_B_prime_CD (A_prime_B_prime_CD_out, op3_prime_out, op2_prime_out, C_op1, D_op0);
  and A_prime_B_prime_CD_prime (A_prime_B_prime_CD_prime_out, A_op3, op2_prime_out, op1_prime_out, op0_prime_out);
  and ABD (ABD_out, A_op3, B_op2, D_op0);
  and A_prime_B_prime_CD_2 (A_prime_B_prime_CD_2_out, op3_prime_out, op2_prime_out, C_op1, D_op0);
  and ACD (LW, A_op3, D_op0, C_op1);
  and ABC_prime_D_prime (SW, A_op3, B_op2, op1_prime_out, op0_prime_out);
  and A_prime_BDC_prime (A_prime_BDC_prime_out, op3_prime_out, B_op2, C_op1, op0_prime_out);
  and A_prime_BCD_prime (A_prime_BCD_prime_out, op3_prime_out, B_op2, C_op1, op0_prime_out);
  and ACD_2 (ACD_2_out, A_op3, C_op1, D_op0);
  and ABD_2 (BEQ, A_op3, B_op2, D_op0);
  and ABC (J, A_op3, B_op2, C_op1);
  and A_prime_C_prime (A_prime_C_prime_out, op3_prime_out, op1_prime_out);
  and A_prime_D_prime (A_prime_D_prime_out, op3_prime_out, op0_prime_out);
  and AB_prime_CD_prime (AB_prime_CD_prime_out, A_op3, op2_prime_out, C_op1, op0_prime_out);
  or or_1 (R_I, AB_prime_D_out, AB_prime_C_out, SW);
  or or_2 (RES_RAM0, A_prime_BCD_prime_out, ACD_2_out);
  or or_3 (WRITE_ENABLE, op2_prime_out, A_prime_C_prime_out, A_prime_D_prime_out);
  or or_4 (ALU_1, AD_out, AC_prime_out, A_prime_B_prime_C_out);
  or or_5 (BIN, AIN, BC_prime_D_out, A_prime_B_prime_CD_out, A_prime_B_prime_CD_prime_out);
  or or_6 (CIN, ABD_out, A_prime_B_prime_CD_2_out, A_prime_B_prime_CD_prime_out);
  or or_7 (RES_RAM1, A_prime_BDC_prime_out, AB_prime_CD_prime_out);
endmodule

module data_with_control (
  input  load,
  input  Clear_PC,
  input  Reg__clr,
  input  [13:0] KEYBOARD,
  output [3:0] Opcode,
  output [2:0] Source_1,
  output [2:0] Source_2,
  output [3:0] Destination_shamt,
  output Shamt,
  output [2:0] destination,
  output [13:0] Data1,
  output Zero,
  output [13:0] ALU_res,
  output Overflow,
  output [13:0] Data1_2,
  output [13:0] Data1_3,
  output [1:0] Data1_4,
  output [13:0] shifted_out
);

  wire AIN, ALU_OP0, ALU_OP1, BEQ, BIN, CIN, Clock_out, J_beq_tunnel, JUMP, LW, or_1_out, or_2_out, R_I, SW,
       WRITE_EN;
  wire [2:0] multiplexer_3_out;
  wire [3:0] a, b, bit_extender_6_out, c, d;
  wire [11:4] rom_1_data;
  wire [13:0] adder_1_out, adder_2_out, bit_extender_1_out, bit_extender_2_out, bit_extender_5_out,
       multiplexer_1_out, multiplexer_2_out, PC_q, ram_1_data;
  wire [13:12] OUT;

  or or_1 (or_1_out, JUMP, J_beq_tunnel);
  Multiplexer #(.width(14), .enable("false")) multiplexer_1 (
    .in0(adder_1_out), .in1(adder_2_out), .out(multiplexer_1_out), .sel(or_1_out));
  Register #(.width(14)) PC (.D(multiplexer_1_out), .Q(PC_q), .clk(Clock_out), .clr(Clear_PC));  // open: en
  Clock Clock (.out(Clock_out));
  Adder #(.width(14)) adder_1 (.a(14'h1), .b(PC_q), .out(adder_1_out));  // open: cin, cout
  Hex_Digit_Display hex_digit_display_1 (.value(a));  // open: dp
  Hex_Digit_Display hex_digit_display_2 (.value(b));  // open: dp
  assign bit_extender_1_out = {{4{1'b0}}, {Source_1, Source_2, destination, Destination_shamt[0]}};  // Bit_Extender bit_extender_1
  assign bit_extender_2_out = {{10{1'b0}}, {destination, Destination_shamt[0]}};  // Bit_Extender bit_extender_2
  Hex_Digit_Display hex_digit_display_3 (.value(c));  // open: dp
  ROM #(.addrWidth(14), .dataWidth(16)) rom_1 (
    .addr(PC_q), .data({Opcode, rom_1_data, destination, Destination_shamt[0]}));  // open: sel
  Hex_Digit_Display hex_digit_display_4 (.value(d));  // open: dp
  Multiplexer #(.width(14), .enable("false")) multiplexer_2 (
    .in0(bit_extender_1_out), .in1(bit_extender_2_out), .out(multiplexer_2_out), .sel(J_beq_tunnel));
  Adder #(.width(14)) adder_2 (.a(adder_1_out), .b(multiplexer_2_out), .out(adder_2_out));  // open: cin, cout
  Bit_Extender #(.in_width(4), .out_width(3)) bit_extender_3 (.in(rom_1_data[11:8]), .out(Source_1));
  Bit_Extender #(.in_width(4), .out_width(3)) bit_extender_4 (.in(rom_1_data[7:4]), .out(Source_2));
  Multiplexer #(.width(3), .enable("false")) multiplexer_3 (
    .in0(destination), .in1(Source_2), .out(multiplexer_3_out), .sel(R_I));
  assign bit_extender_5_out = {{10{1'b0}}, {destination, Destination_shamt[0]}};  // Bit_Extender bit_extender_5
  _14_bit_register_file u_14_bit_register_file_1 (
    .Write_Data(Data1_2), .Write_enabler(WRITE_EN), .RT_Selector(Source_2), .Register_CLOCK(Clock_out),
    .RD_Selector(multiplexer_3_out), .Data_1_Out(Data1), .RS_Selector(Source_1), .Data_2_Out({OUT, b, c, d}),
    .Register_CLEAR(Reg__clr));
  assign bit_extender_6_out = {{3{1'b0}}, Destination_shamt[0]};  // Bit_Extender bit_extender_6
  Multiplexer #(.width(14), .enable("false")) multiplexer_4 (
    .in0({OUT, b, c, d}), .in1(bit_extender_5_out), .out(Data1_3), .sel(R_I));
  control_2 control_2_1 (
    .ALU_1(ALU_OP1), .ALU_0(ALU_OP0), .AIN(AIN), .BIN(BIN), .CIN(CIN), .LW(LW), .SW(SW),
    .RES_RAM1(Data1_4[1]), .RES_RAM0(Data1_4[0]), .BEQ(BEQ), .J(JUMP), .WRITE_ENABLE(WRITE_EN),
    .A_op3(Opcode[3]), .B_op2(Opcode[2]), .C_op1(Opcode[1]), .D_op0(Opcode[0]), .R_I(R_I));
  // Probe on Data1
  // Probe on Data1_3
  _14_bit_ALU u_14_bit_alu_1 (
    .a(Data1), .b(Data1_3), .Operation({ALU_OP1, ALU_OP0}), .Ain(AIN), .Bin(BIN), .S(ALU_res),
    .Zero_Signal(Zero), .out_9(Overflow), .Cin(CIN));
  Shifter #(.width(14)) shifter_1 (.in(Data1), .\dist (bit_extender_6_out), .out(shifted_out));
  and beq_cont (J_beq_tunnel, BEQ, Zero);
  // Probe on ALU_res
  or or_2 (or_2_out, SW, LW);
  RAM #(.addrWidth(14), .dataWidth(14), .bus("separate")) ram_1 (
    .addr(ALU_res), .din({OUT, b, c, d}), .data(ram_1_data), .str(SW), .sel(or_2_out), .clk(Clock_out),
    .ld(LW));  // open: clr
  Multiplexer #(.select(2), .width(14), .enable("false")) multiplexer_5 (
    .in0(ALU_res), .in1(ram_1_data), .in2(shifted_out), .in3(KEYBOARD), .out(Data1_2), .sel(Data1_4));
  // Probe on Data1_2
  assign a = {{2{1'b0}}, OUT};  // Bit_Extender bit_extender_7

  assign Destination_shamt[3:1] = destination;
  assign Shamt = Destination_shamt[0];

  // Other names for the same wires on the sheet: OUT[11:0] = {b, c, d}; RES_RAM[1:0] = Data1_4

  // Notes on the sheet:
  //   contents of rom_1 (hex, n*v repeats v):
  //   d125 d125 d125 0 2 0 3e01
endmodule

module DATA_SHOFTER (
  input  Clear_PC,
  input  R_I,
  input  Reg__clr,
  input  [13:0] KEYBOARD,
  output [3:0] Opcode,
  output [2:0] Source_1,
  output [2:0] Source_2,
  output [2:0] destination,
  output Shamt,
  output [13:0] Data1,
  output Zero,
  output [13:0] ALU_res,
  output Overflow,
  output [13:0] Data1_2,
  output [13:0] Data1_3
);

  wire AIN, ALU_OP0, ALU_OP1, BEQ, beq_cont_out, BIN, CIN, Clock_out, JUMP, LW, or_1_out, R_I_t, SW, WRITE_EN;
  wire [1:0] RES_RAM;
  wire [2:0] multiplexer_2_out;
  wire [3:0] a, b, bit_extender_5_out, c, d;
  wire [11:4] rom_1_data;
  wire [13:0] adder_1_out, adder_2_out, bit_extender_1_out, bit_extender_4_out, multiplexer_1_out,
       multiplexer_3_out, multiplexer_5_out, PC_q, shifter_1_out;
  wire [13:12] OUT;

  Multiplexer #(.width(14), .enable("false")) multiplexer_1 (
    .in0(adder_1_out), .in1(multiplexer_3_out), .out(multiplexer_1_out), .sel(JUMP));
  Register #(.width(14)) PC (.D(multiplexer_1_out), .Q(PC_q), .clk(Clock_out), .clr(Clear_PC));  // open: en
  Clock Clock (.out(Clock_out));
  Adder #(.width(14)) adder_1 (.a(14'h1), .b(PC_q), .out(adder_1_out));  // open: cin, cout
  ROM #(.addrWidth(14), .dataWidth(16)) rom_1 (
    .addr(PC_q), .data({Opcode, rom_1_data, destination, Shamt}));  // open: sel
  assign bit_extender_1_out = {{4{1'b0}}, {Source_1, Source_2, destination, Shamt}};  // Bit_Extender bit_extender_1
  Adder #(.width(14)) adder_2 (.a(adder_1_out), .b(bit_extender_1_out), .out(adder_2_out));  // open: cin, cout
  Bit_Extender #(.in_width(4), .out_width(3)) bit_extender_2 (.in(rom_1_data[11:8]), .out(Source_1));
  Bit_Extender #(.in_width(4), .out_width(3)) bit_extender_3 (.in(rom_1_data[7:4]), .out(Source_2));
  Multiplexer #(.width(3), .enable("false")) multiplexer_2 (
    .in0(destination), .in1(Source_2), .out(multiplexer_2_out), .sel(R_I_t));
  assign bit_extender_4_out = {{11{1'b0}}, {destination[1:0], Shamt}};  // Bit_Extender bit_extender_4
  Multiplexer #(.width(14), .enable("false")) multiplexer_3 (
    .in0(adder_1_out), .in1(adder_2_out), .out(multiplexer_3_out), .sel(beq_cont_out));
  _14_bit_register_file u_14_bit_register_file_1 (
    .Write_Data(multiplexer_5_out), .Write_enabler(WRITE_EN), .RT_Selector(Source_2),
    .Register_CLOCK(Clock_out), .RD_Selector(multiplexer_2_out), .Data_1_Out(Data1), .RS_Selector(Source_1),
    .Data_2_Out({OUT, b, c, d}), .Register_CLEAR(Reg__clr));
  Multiplexer #(.width(14), .enable("false")) multiplexer_4 (
    .in0({OUT, b, c, d}), .in1(bit_extender_4_out), .out(Data1_3), .sel(R_I));
  or or_1 (or_1_out, destination[2], BIN);
  control_2 control_2_1 (
    .ALU_1(ALU_OP1), .ALU_0(ALU_OP0), .AIN(AIN), .BIN(BIN), .CIN(CIN), .LW(LW), .SW(SW),
    .RES_RAM1(RES_RAM[1]), .RES_RAM0(RES_RAM[0]), .BEQ(BEQ), .J(JUMP), .WRITE_ENABLE(WRITE_EN),
    .A_op3(Opcode[3]), .B_op2(Opcode[2]), .C_op1(Opcode[1]), .D_op0(Opcode[0]), .R_I(R_I_t));
  // Probe on Data1
  // Probe on Data1_3
  _14_bit_ALU u_14_bit_alu_1 (
    .a(Data1), .b(Data1_3), .Operation({ALU_OP1, ALU_OP0}), .Ain(AIN), .Bin(or_1_out), .S(ALU_res),
    .Zero_Signal(Zero), .out_9(Overflow), .Cin(CIN));
  Bit_Extender #(.in_width(14), .out_width(4)) bit_extender_5 (.in(bit_extender_4_out), .out(bit_extender_5_out));
  and beq_cont (beq_cont_out, BEQ, Zero);
  // Probe on ALU_res
  Shifter #(.width(14)) shifter_1 (.in(Data1), .\dist (bit_extender_5_out), .out(shifter_1_out));
  Hex_Digit_Display hex_digit_display_1 (.value(a));  // open: dp
  Hex_Digit_Display hex_digit_display_2 (.value(b));  // open: dp
  RAM #(.addrWidth(14), .dataWidth(14), .bus("separate")) ram_1 (
    .addr(ALU_res), .din({OUT, b, c, d}), .data(Data1_2), .str(SW), .clk(Clock_out), .ld(LW));  // open: sel, clr
  Hex_Digit_Display hex_digit_display_3 (.value(d));  // open: dp
  Hex_Digit_Display hex_digit_display_4 (.value(c));  // open: dp
  // Probe on Data1_2
  Multiplexer #(.select(2), .width(14), .enable("false")) multiplexer_5 (
    .in0(ALU_res), .in1(Data1_2), .in2(shifter_1_out), .in3(KEYBOARD), .out(multiplexer_5_out), .sel(RES_RAM));
  assign a = {{2{1'b0}}, OUT};  // Bit_Extender bit_extender_6

  // Other names for the same wires on the sheet: OUT[11:0] = {b, c, d}; SHIFT[13:0] = Data1

  // Notes on the sheet:
  //   contents of rom_1 (hex, n*v repeats v):
  //   a525 a52f 7020 8538 236e 8535 8538 7040 7050 8538 9535 a531 b454 c543 d535 e003 7030
endmodule

module _1_alu_copy (
  input  a,
  input  Ain,
  input  Cin_for_adder,
  input  b,
  input  [1:0] ALU_Op,
  input  Bin,
  input  Less,
  output out_8,
  output set,
  output out_10
);

  wire and_1_out, multiplexer_1_out, multiplexer_2_out, not_1_out, not_2_out, or_1_out;

  not not_1 (not_1_out, a);
  not not_2 (not_2_out, b);
  Multiplexer #(.enable("false")) multiplexer_1 (.in0(a), .in1(not_1_out), .out(multiplexer_1_out), .sel(Ain));
  Multiplexer #(.enable("false")) multiplexer_2 (.in0(b), .in1(not_2_out), .out(multiplexer_2_out), .sel(Bin));
  and and_1 (and_1_out, multiplexer_1_out, multiplexer_2_out);
  or or_1 (or_1_out, multiplexer_1_out, multiplexer_2_out);
  Adder #(.width(1)) adder_1 (
    .a(multiplexer_1_out), .b(multiplexer_2_out), .out(set), .cin(Cin_for_adder), .cout(out_10));
  Multiplexer #(.select(2), .enable("false")) multiplexer_3 (
    .in0(and_1_out), .in1(or_1_out), .in2(set), .in3(Less), .out(out_8), .sel(ALU_Op));
endmodule

module CONTROL_3 (
  input  A_op3,
  input  B_op2,
  input  C_op1,
  input  D_op0,
  output ALU_1,
  output ALU_0,
  output AIN,
  output BIN,
  output CIN,
  output LW,
  output SW,
  output RES_RAM1,
  output RES_RAM0,
  output BEQ,
  output J,
  output WRITE_ENABLE,
  output R_I
);

  wire A_prime_B_prime_C_out, A_prime_B_prime_CD_2_out, A_prime_B_prime_CD_out, A_prime_B_prime_CD_prime_out,
       A_prime_BDC_prime_out, A_prime_C_prime_out, A_prime_D_prime_out, AB_prime_C_out,
       AB_prime_CD_prime_out, AB_prime_D_out, ABCD_prime_out, ABD_out, AC_prime_out, ACD_2_out, AD_out,
       BC_prime_D_out, op0_prime_out, op1_prime_out, op2_prime_out, op3_prime_out;

  not op3_prime (op3_prime_out, A_op3);
  not op2_prime (op2_prime_out, B_op2);
  not op1_prime (op1_prime_out, C_op1);
  not op0_prime (op0_prime_out, D_op0);
  and AB_prime_D (AB_prime_D_out, A_op3, op2_prime_out, op0_prime_out);
  and AB_prime_C (AB_prime_C_out, A_op3, op2_prime_out, C_op1);
  and AD (AD_out, A_op3, D_op0);
  // AND_Gate AC has open pins: in0=A_op3, in1=C_op1, out=open
  // AND_Gate AB has open pins: in0=A_op3, in1=B_op2, out=open
  and AC_prime (AC_prime_out, A_op3, op1_prime_out);
  and A_prime_B_prime_C (A_prime_B_prime_C_out, op3_prime_out, op2_prime_out, C_op1);
  and A_prime_C_prime_D (ALU_0, op3_prime_out, op1_prime_out, D_op0);
  and A_prime_BC_prime (AIN, op3_prime_out, B_op2, op1_prime_out);
  and BC_prime_D (BC_prime_D_out, B_op2, op1_prime_out, D_op0);
  and A_prime_B_prime_CD (A_prime_B_prime_CD_out, op3_prime_out, op2_prime_out, C_op1, D_op0);
  and A_prime_B_prime_CD_prime (A_prime_B_prime_CD_prime_out, A_op3, op2_prime_out, op1_prime_out, op0_prime_out);
  and ABD (ABD_out, A_op3, B_op2, D_op0);
  and A_prime_B_prime_CD_2 (A_prime_B_prime_CD_2_out, op3_prime_out, op2_prime_out, C_op1, D_op0);
  and ACD (LW, A_op3, D_op0, C_op1);
  and ABC_prime_D_prime (SW, A_op3, B_op2, op1_prime_out, op0_prime_out);
  and A_prime_BDC_prime (A_prime_BDC_prime_out, op3_prime_out, B_op2, C_op1, op0_prime_out);
  and ABCD_prime (ABCD_prime_out, A_op3, B_op2, C_op1, op0_prime_out);
  and ACD_2 (ACD_2_out, A_op3, C_op1, D_op0);
  and ABD_2 (BEQ, A_op3, B_op2, D_op0);
  and ABC (J, A_op3, B_op2, C_op1);
  and A_prime_C_prime (A_prime_C_prime_out, op3_prime_out, op1_prime_out);
  and A_prime_D_prime (A_prime_D_prime_out, op3_prime_out, op0_prime_out);
  and AB_prime_CD_prime (AB_prime_CD_prime_out, A_op3, op2_prime_out, C_op1, op0_prime_out);
  or or_1 (R_I, AB_prime_D_out, AB_prime_C_out, SW);
  or or_2 (RES_RAM0, ABCD_prime_out, ACD_2_out);
  or or_3 (WRITE_ENABLE, op2_prime_out, A_prime_C_prime_out, A_prime_D_prime_out);
  or or_4 (ALU_1, AD_out, AC_prime_out, A_prime_B_prime_C_out);
  or or_5 (BIN, AIN, BC_prime_D_out, A_prime_B_prime_CD_out, A_prime_B_prime_CD_prime_out);
  or or_6 (CIN, ABD_out, A_prime_B_prime_CD_2_out, A_prime_B_prime_CD_prime_out);
  or or_7 (RES_RAM1, A_prime_BDC_prime_out, AB_prime_CD_prime_out);
endmodule

module v6 (
  input  load,
  input  Clear_PC,
  input  Reg__clr,
  input  [13:0] KEYBOARD,
  output [3:0] Opcode,
  output [2:0] Source_1,
  output [2:0] Source_2,
  output [3:0] Destination_shamt,
  output Shamt,
  output [2:0] destination,
  output [13:0] Data1,
  output Zero,
  output [13:0] ALU_res,
  output Overflow,
  output [13:0] Data1_2,
  output [13:0] Data1_3,
  output [1:0] Data1_4,
  output [13:0] shifted_out
);

  wire AIN, ALU_OP0, ALU_OP1, BEQ, BIN, CIN, Clock_out, J_beq_tunnel, JUMP, LW, or_1_out, or_2_out, R_I, SW,
       WRITE_EN;
  wire [2:0] multiplexer_3_out;
  wire [3:0] a, b, bit_extender_6_out, c, d;
  wire [11:4] rom_1_data;
  wire [13:0] adder_1_out, adder_2_out, bit_extender_1_out, bit_extender_2_out, bit_extender_5_out,
       multiplexer_1_out, multiplexer_2_out, PC_q, ram_1_data;
  wire [13:12] OUT;

  or or_1 (or_1_out, JUMP, J_beq_tunnel);
  Multiplexer #(.width(14), .enable("false")) multiplexer_1 (
    .in0(adder_1_out), .in1(multiplexer_2_out), .out(multiplexer_1_out), .sel(or_1_out));
  Register #(.width(14)) PC (.D(multiplexer_1_out), .Q(PC_q), .clk(Clock_out), .clr(Clear_PC));  // open: en
  Clock Clock (.out(Clock_out));
  assign bit_extender_1_out = {{10{1'b0}}, {destination, Destination_shamt[0]}};  // Bit_Extender bit_extender_1
  Adder #(.width(14)) adder_1 (.a(14'h1), .b(PC_q), .out(adder_1_out));  // open: cin, cout
  Hex_Digit_Display hex_digit_display_1 (.value(a));  // open: dp
  Hex_Digit_Display hex_digit_display_2 (.value(b));  // open: dp
  assign bit_extender_2_out = {{4{1'b0}}, {Source_1, Source_2, destination, Destination_shamt[0]}};  // Bit_Extender bit_extender_2
  Adder #(.width(14)) adder_2 (.a(adder_1_out), .b(bit_extender_1_out), .out(adder_2_out));  // open: cin, cout
  Hex_Digit_Display hex_digit_display_3 (.value(c));  // open: dp
  ROM #(.addrWidth(14), .dataWidth(16)) rom_1 (
    .addr(PC_q), .data({Opcode, rom_1_data, destination, Destination_shamt[0]}));  // open: sel
  Hex_Digit_Display hex_digit_display_4 (.value(d));  // open: dp
  Multiplexer #(.width(14), .enable("false")) multiplexer_2 (
    .in0(bit_extender_2_out), .in1(adder_2_out), .out(multiplexer_2_out), .sel(J_beq_tunnel));
  Bit_Extender #(.in_width(4), .out_width(3)) bit_extender_3 (.in(rom_1_data[11:8]), .out(Source_1));
  Bit_Extender #(.in_width(4), .out_width(3)) bit_extender_4 (.in(rom_1_data[7:4]), .out(Source_2));
  Multiplexer #(.width(3), .enable("false")) multiplexer_3 (
    .in0(destination), .in1(Source_2), .out(multiplexer_3_out), .sel(R_I));
  assign bit_extender_5_out = {{10{1'b0}}, {destination, Destination_shamt[0]}};  // Bit_Extender bit_extender_5
  _14_bit_register_file u_14_bit_register_file_1 (
    .Write_Data(Data1_2), .Write_enabler(WRITE_EN), .RT_Selector(Source_2), .Register_CLOCK(Clock_out),
    .RD_Selector(multiplexer_3_out), .Data_1_Out(Data1), .RS_Selector(Source_1), .Data_2_Out({OUT, b, c, d}),
    .Register_CLEAR(Reg__clr));
  assign bit_extender_6_out = {{3{1'b0}}, Destination_shamt[0]};  // Bit_Extender bit_extender_6
  Multiplexer #(.width(14), .enable("false")) multiplexer_4 (
    .in0({OUT, b, c, d}), .in1(bit_extender_5_out), .out(Data1_3), .sel(R_I));
  control_2 control_2_1 (
    .ALU_1(ALU_OP1), .ALU_0(ALU_OP0), .AIN(AIN), .BIN(BIN), .CIN(CIN), .LW(LW), .SW(SW),
    .RES_RAM1(Data1_4[1]), .RES_RAM0(Data1_4[0]), .BEQ(BEQ), .J(JUMP), .WRITE_ENABLE(WRITE_EN),
    .A_op3(Opcode[3]), .B_op2(Opcode[2]), .C_op1(Opcode[1]), .D_op0(Opcode[0]), .R_I(R_I));
  // Probe on Data1
  // Probe on Data1_3
  _14_bit_ALU u_14_bit_alu_1 (
    .a(Data1), .b(Data1_3), .Operation({ALU_OP1, ALU_OP0}), .Ain(AIN), .Bin(BIN), .S(ALU_res),
    .Zero_Signal(Zero), .out_9(Overflow), .Cin(CIN));
  Shifter #(.width(14)) shifter_1 (.in(Data1), .\dist (bit_extender_6_out), .out(shifted_out));
  and beq_cont (J_beq_tunnel, BEQ, Zero);
  // Probe on ALU_res
  or or_2 (or_2_out, SW, LW);
  RAM #(.addrWidth(14), .dataWidth(14), .bus("separate")) ram_1 (
    .addr(ALU_res), .din({OUT, b, c, d}), .data(ram_1_data), .str(SW), .sel(or_2_out), .clk(Clock_out),
    .ld(LW));  // open: clr
  Multiplexer #(.select(2), .width(14), .enable("false")) multiplexer_5 (
    .in0(ALU_res), .in1(ram_1_data), .in2(shifted_out), .in3(KEYBOARD), .out(Data1_2), .sel(Data1_4));
  // Probe on Data1_2
  assign a = {{2{1'b0}}, OUT};  // Bit_Extender bit_extender_7

  assign Destination_shamt[3:1] = destination;
  assign Shamt = Destination_shamt[0];

  // Other names for the same wires on the sheet: OUT[11:0] = {b, c, d}; RES_RAM[1:0] = Data1_4

  // Notes on the sheet:
  //   contents of rom_1 (hex, n*v repeats v):
  //   9667 9773 9440 367c 9110 d163 2418 9111 e005 7040 0 0 7040
endmodule
